# Fritzing sketch valve (saved by Fritzing 0.9.3b)
breadboards: 1

parts:
  Raspberry_Pi_Zero1 = Raspberry Pi Zero
  L1 = Solenoid
  Q1 = NPN-Transistor [package="TO92 [THT]"]
  VCC1 = Battery block 9V
  D1 = Rectifier Diode [part_number=1N4001 package="Melf DO-213 AB [SMD]"]
  R1 = Resistor [tolerance=±5% resistance=1k package="2010 [SMD]"]

nets:
  N1: Raspberry_Pi_Zero1.GND, Q1.C, VCC1.-
  N2: Raspberry_Pi_Zero1.GPIO18, R1.Pin_0
  N3: L1.pin1, Q1.B, D1.anode
  N4: L1.pin2, VCC1.+, D1.cathode
  N5: Q1.E, R1.Pin_1
